# Fritzing sketch wiring_v1 (saved by Fritzing 0.9.6b)
breadboards: 2

parts:
  Mod1 = Raspberry Pi Pico
  Part1 = Adafruit DRV8833 DC/Stepper Motor Driver [part_number="Adafruit #3297"]
  Part2 = Adafruit DRV8833 DC/Stepper Motor Driver [part_number="Adafruit #3297"]
  Part3 = InvenSense MPU6050
  Part4 = PowerBoost 500 Charger
  U1 = LIPO-2000mAh [package=lipo-2000]  # not connected
  M1 = DC Motor
  M3 = DC Motor
  M4 = DC Motor
  M5 = DC Motor

nets:
  GND: Mod1.pin_3, Mod1.pin_8, Mod1.pin_13, Mod1.pin_18, Mod1.pin_23, Mod1.pin_28, Mod1.pin_33, Mod1.pin_38, Part1.GND, Part2.GND, Part3.GND, Part4.GND
  N1: Mod1.pin_14, Part1.AIN1
  N2: Mod1.pin_15, Part1.AIN2
  N3: Mod1.pin_16, Part1.BIN1
  N4: Mod1.pin_17, Part1.BIN2
  N5: Mod1.pin_19, Part3.SDA
  N6: Mod1.pin_20, Part3.SCL
  N7: Mod1.pin_24, Part2.AIN1
  N8: Mod1.pin_25, Part2.AIN2
  N9: Mod1.pin_26, Part2.BIN1
  N10: Mod1.pin_27, Part2.BIN2
  N11: Mod1.pin_36, Part1.!SLEEP, Part2.!SLEEP, Part3.VCC
  N12: Mod1.pin_39, Part4.VBAT
  N13: Part1.PWRIN, Part2.PWRIN, Part4.5.0V
  N14: Part1.AOUT2, M5.pin_2
  N15: Part1.AOUT1, M5.pin_1
  N16: Part1.BOUT1, M3.pin_1
  N17: Part1.BOUT2, M3.pin_2
  N18: Part2.AOUT2, M4.pin_2
  N19: Part2.AOUT1, M4.pin_1
  N20: Part2.BOUT1, M1.pin_1
  N21: Part2.BOUT2, M1.pin_2

custom parts:
  Raspberry Pi Pico: Raspberry Pi Pico. Based around the RP2040 microcontroller the Pico is a low cost microcontroller device bringing Raspberry Pi quality, cost, and easy of use to the microcontroller space. Jan 2021, Split part in to two versions: tht (this one) and SMD. This one will drill holes for a .1 in header in pcb to allow plugging in the module as well as providing pads to solder the module to the top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
  Adafruit DRV8833 DC/Stepper Motor Driver: Spin two DC motors or step one bi-polar or uni-polar stepper with up to 1.2A per channel using the DRV8833. This motor driver chip is a nice alternative to the TB6612 driver. Like that chip, you get 2 full H-bridges, but this chip is better for low voltage uses (can run from 2.7V up to 10.8V motor power) and has built in current limiting capability. We set it up for 1A current limiting so you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
  PowerBoost 500 Charger: The PowerBoost 500C is a little DC/DC boost converter module that can be powered by any 3.7V LiIon/LiPoly battery, and convert the battery output to 5.2V DC for running your 5V projects. At its heart is a TPS61090 boost converter from TI. This boost converter chip has some really nice extras such as low battery detection, 2A internal switch, synchronous conversion, excellent efficiency, and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
