# Fritzing sketch wiring_v2 (saved by Fritzing 0.9.6b)
breadboards: 2

parts:
  Mod1 = Raspberry Pi Pico
  Part3 = InvenSense MPU6050
  U1 = LIPO-2000mAh [package=lipo-2000]
  M1 = DC Motor
  M3 = DC Motor
  M4 = DC Motor
  M5 = DC Motor
  Part5 = Adafruit TB6612 DC and Stepper Motor Driver [part_number="Adafruit #2448"]
  Part6 = Adafruit TB6612 DC and Stepper Motor Driver [part_number="Adafruit #2448"]

nets:
  GND: Mod1.pin_3, Mod1.pin_8, Mod1.pin_13, Mod1.pin_18, Mod1.pin_23, Mod1.pin_28, Mod1.pin_33, Mod1.pin_38, Mod1.pin_42, Part3.GND, U1.-, Part5.GND, Part6.GND
  N1: Mod1.pin_14, Part5.AIN2
  N2: Mod1.pin_15, Part5.AIN1
  N3: Mod1.pin_16, Part5.BIN2
  N4: Mod1.pin_17, Part5.BIN1
  N5: Mod1.pin_19, Part3.SDA
  N6: Mod1.pin_20, Part3.SCL
  N7: Mod1.pin_21, Part6.PWMA
  N8: Mod1.pin_22, Part6.PWMB
  N9: Mod1.pin_24, Part6.AIN2
  N10: Mod1.pin_25, Part6.AIN1
  N11: Mod1.pin_26, Part6.BIN2
  N12: Mod1.pin_27, Part6.BIN1
  N13: Mod1.pin_31, Part5.PWMB
  N14: Mod1.pin_32, Part5.PWMA
  VCC: Mod1.pin_36, Part3.VCC, Part5.VCC, Part5.STBY, Part6.VCC, Part6.STBY
  N15: Mod1.pin_39, U1.+, Part5.PWRIN, Part6.PWRIN
  N16: M1.pin_1, Part6.MOTORB1
  N17: M1.pin_2, Part6.MOTORB2
  N18: M3.pin_1, Part5.MOTORB1
  N19: M3.pin_2, Part5.MOTORB2
  N20: M4.pin_1, Part6.MOTORA1
  N21: M4.pin_2, Part6.MOTORA2
  N22: M5.pin_1, Part5.MOTORA1
  N23: M5.pin_2, Part5.MOTORA2

custom parts:
  Raspberry Pi Pico: Raspberry Pi Pico. Based around the RP2040 microcontroller the Pico is a low cost microcontroller device bringing Raspberry Pi quality, cost, and easy of use to the microcontroller space. Jan 2021, Split part in to two versions: tht (this one) and SMD. This one will drill holes for a .1 in header in pcb to allow plugging in the module as well as providing pads to solder the module to the top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
  Adafruit TB6612 DC and Stepper Motor Driver: Spin two DC motors, step one bi-polar or uni-polar stepper, or fire off two solenoids with 1.2A per channel using the TB6612. These are perhaps better known as "the drivers in our assembled Adafruit Motorshield or Motor HAT." We really like these dual H-bridges, so if you want to control motors without a shield or HAT these are easy to include on any solderless breadboard or perma-proto.
