# Fritzing sketch wiring_v3 (saved by Fritzing 0.9.6b)
breadboards: 2

parts:
  Mod1 = Raspberry Pi Pico
  Part3 = InvenSense MPU6050
  U1 = LIPO-2000mAh [package=lipo-2000]
  M1 = DC Motor
  M3 = DC Motor
  M4 = DC Motor
  M5 = DC Motor
  Q1 = Basic FET N-Channel [package="D2Pak [SMD]"]
  Q2 = Basic FET N-Channel [package="D2Pak [SMD]"]
  Q3 = Basic FET N-Channel [package="D2Pak [SMD]"]
  Q4 = Basic FET N-Channel [package="D2Pak [SMD]"]

nets:
  N1: Mod1.pin_3, Mod1.pin_8, Mod1.pin_13, Mod1.pin_18, Mod1.pin_23, Mod1.pin_28, Mod1.pin_33, Mod1.pin_38, Mod1.pin_42, Part3.GND, U1.-, Q1.source, Q2.source, Q3.source, Q4.source
  N2: Mod1.pin_14, Q2.Gate
  N3: Mod1.pin_15, Q3.Gate
  N4: Mod1.pin_16, Q1.Gate
  N5: Mod1.pin_17, Q4.Gate
  N6: Mod1.pin_19, Part3.SDA
  N7: Mod1.pin_20, Part3.SCL
  N8: Mod1.pin_36, Part3.VCC
  N9: Mod1.pin_39, U1.+, M1.pin_2, M3.pin_2, M4.pin_2, M5.pin_2
  N10: M1.pin_1, Q4.drain
  N11: M3.pin_1, Q3.drain
  N12: M4.pin_1, Q1.drain
  N13: M5.pin_1, Q2.drain

custom parts:
  Raspberry Pi Pico: Raspberry Pi Pico. Based around the RP2040 microcontroller the Pico is a low cost microcontroller device bringing Raspberry Pi quality, cost, and easy of use to the microcontroller space. Jan 2021, Split part in to two versions: tht (this one) and SMD. This one will drill holes for a .1 in header in pcb to allow plugging in the module as well as providing pads to solder the module to the top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
